# Fritzing sketch sketch (saved by Fritzing 0.9.3b)
breadboards: 1

parts:
  Raspberry_Pi_B_rev1 = Raspberry Pi B rev1
  DHT1 = DHT22 Humidity and Temperature Sensor
  R1 = Resistor [tolerance=±5% resistance=4.7k package="0805 [SMD]"]

nets:
  5V: Raspberry_Pi_B_rev1.5V, DHT1.VDD, R1.Pin_0
  GND: Raspberry_Pi_B_rev1.GND, DHT1.GND
  N1: Raspberry_Pi_B_rev1.GPIO_4, DHT1.DATA, R1.Pin_1
